# Fritzing sketch projet3 (saved by Fritzing 0.9.5d)
circuit board: 8.46667cm x 5.64444cm
breadboards: 1

parts:
  Composant1 = Arduino Uno (Rev3)
  LED1 = LED - 5mm [color="Orange (620nm)" package="5 mm [THT]"]
  R1 = Resistor [tolerance=±5% resistance=220 package=THT]
  S1 = SWITCH-MOMENTARY-2 [package=tactile-pth-12mm]
  R2 = Resistor [tolerance=±5% resistance=220 package=THT]

nets:
  N1: Composant1.GND, R1.Pin_1, R2.Pin_0
  N2: Composant1.D2, LED1.anode
  N3: Composant1.D3_PWM, S1.2, R2.Pin_1
  N4: Composant1.5V, S1.1
  N5: LED1.cathode, R1.Pin_0
