# Fritzing sketch projet5a (saved by Fritzing 0.9.5d)
circuit board: 8.46667cm x 5.64444cm
breadboards: 1

parts:
  Composant1 = Arduino Uno (Rev3)
  LED1 = LED - 5mm [color="Orange (620nm)" package="5 mm [THT]"]
  R1 = Resistor [tolerance=±5% resistance=220 package=THT]
  R2 = Resistor [tolerance=±5% resistance=1k package=THT]
  R3 = Resistor [tolerance=±5% resistance=680 package=THT]
  R4 = Resistor [tolerance=±5% resistance=6.8k package=THT]

nets:
  N1: Composant1.A0, R2.Pin_1, R3.Pin_1
  N2: Composant1.A1, LED1.anode
  N3: Composant1.GND, R1.Pin_1, R3.Pin_0
  N4: LED1.cathode, R1.Pin_0
  N5: R2.Pin_0, R4.Pin_1
  + 31V max: R4.Pin_0

notes:
  Req. = 7.8KΩ
