# Fritzing sketch projet5b (saved by Fritzing 0.9.5d)
circuit board: 6.88566cm x 5.36311cm
breadboards: 1

parts:
  R3 = Resistor [resistance=2.2k tolerance=±5% package=THT]
  Arduino2 = Arduino Uno (Rev3)
  R4 = Resistor [resistance=1k tolerance=±5% package=THT]

nets:
  N1: R3.Pin_0, Arduino2.GND
  N2: R3.Pin_1, Arduino2.A3, R4.Pin_0
  N3: Arduino2.5V, R4.Pin_1
