# Fritzing sketch projet7a (saved by Fritzing 0.9.5d)
breadboards: 1

parts:
  Composant1 = Arduino Uno (Rev3)
  Composant2 = Adafruit DS1307 RTC Breakout [part_number="Adafruit #264"]
  R1 = Resistor [tolerance=±5% resistance=1k package=THT]
  R2 = Resistor [tolerance=±5% resistance=1k package=THT]
  DS2 = DS18B20 1-Wire Temperature Sensor [part_number=DS18B20]

nets:
  N1: Composant1.A5/SCL, Composant2.SQW, R2.Pin_1
  N2: Composant1.A4/SDA, Composant2.SCL, R1.Pin_1
  N3: Composant1.D5_PWM, DS2.DQ
  5V: Composant1.5V, Composant2.VCC, R1.Pin_0, R2.Pin_0, DS2.VDD
  GND: Composant1.GND, Composant2.GND, DS2.GND

custom parts:
  Adafruit DS1307 RTC Breakout: This is a great battery-backed real time clock (RTC) that allows your microcontroller project to keep track of time even if it is reprogrammed, or if the power is lost. Perfect for datalogging, clock-building, time stamping, timers and alarms, etc. The DS1307 is the most popular RTC - but it requires 5V power to work (although we've used it with 5V power and 3.3V logic successfully) PCB &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
